// Logisim project 05-move-selection.circ as structural Verilog: 1 circuit, main circuit main
module main (
);

  // AND_Gate and_1 is placed but not wired
  // NOT_Gate not_1 is placed but not wired
endmodule
