// Logisim project 10-tool-attributes.circ as structural Verilog: 1 circuit, main circuit main
module main (
);

  // AND_Gate and_1 is placed but not wired
  // AND_Gate and_2 is placed but not wired
endmodule
