// Logisim project bubbletree-fixture.circ as structural Verilog: 3 circuits, main circuit top
module leaf (
);

  Button press ();  // open: out
  LED lamp ();  // open: in
endmodule

module middle (
);

  LED midlamp ();  // open: in
  leaf inner ();
  leaf other ();
endmodule

module top (
);

  _7_Segment_Display digit ();  // open: g, f, a, b, e, d, c, dp
  middle first ();
  middle second ();
  leaf bare ();
endmodule
